// Logisim project basic_xor_encryption.circ as structural Verilog: 1 circuit, main circuit main
module main (
  input  [7:0] Key,
  input  [7:0] Key_2,
  input  [7:0] Data,
  input  [7:0] Cypher,
  output [7:0] Cypher_2,
  output [7:0] Data_2
);

  xor xor_1 (Cypher_2[0], Key[0], Data[0]);
  xor xor_2 (Cypher_2[1], Key[1], Data[1]);
  xor xor_3 (Cypher_2[2], Key[2], Data[2]);
  xor xor_4 (Cypher_2[3], Key[3], Data[3]);
  xor xor_5 (Cypher_2[4], Key[4], Data[4]);
  xor xor_6 (Cypher_2[5], Key[5], Data[5]);
  xor xor_7 (Cypher_2[6], Key[6], Data[6]);
  xor xor_8 (Cypher_2[7], Key[7], Data[7]);
  xor xor_9 (Data_2[0], Key_2[0], Cypher[0]);
  xor xor_10 (Data_2[1], Key_2[1], Cypher[1]);
  xor xor_11 (Data_2[2], Key_2[2], Cypher[2]);
  xor xor_12 (Data_2[3], Key_2[3], Cypher[3]);
  xor xor_13 (Data_2[4], Key_2[4], Cypher[4]);
  xor xor_14 (Data_2[5], Key_2[5], Cypher[5]);
  xor xor_15 (Data_2[6], Key_2[6], Cypher[6]);
  xor xor_16 (Data_2[7], Key_2[7], Cypher[7]);

  // Notes on the sheet:
  //   Encrypt
  //   Decrypt
endmodule
