// Logisim project latches.circ as structural Verilog: 1 circuit, main circuit main
module main (
  input  S,
  input  S_2,
  input  R,
  input  S_3,
  input  E,
  input  R_2,
  input  S_4,
  input  E_2,
  input  R_3,
  output Q,
  output t,
  output Q_2,
  output t_2,
  output Q_3,
  output t_3,
  output Q_4
);

  wire and_1_out, and_2_out, and_3_out, and_4_out, and_5_out, not_1_out;

  not not_1 (not_1_out, S_4);
  or or_1 (Q, S, Q);
  nor nor_1 (t, S_2, Q_2);
  nor nor_2 (Q_2, t, R);
  and and_1 (and_1_out, S_3, E);
  nor nor_3 (t_2, and_1_out, Q_3);
  nor nor_4 (Q_3, t_2, and_2_out);
  and and_2 (and_2_out, E, R_2);
  and and_3 (and_3_out, S_4, E_2);
  and and_4 (and_4_out, E_2, and_5_out);
  and and_5 (and_5_out, not_1_out, R_3);
  nor nor_5 (t_3, and_3_out, Q_4);
  nor nor_6 (Q_4, t_3, and_4_out);

  // Notes on the sheet:
  //   Latch
  //   SR Latch
  //   Sensible SR Latch
  //   SR Latch Type D
endmodule
