// Logisim project logic_gate_test.circ as structural Verilog: 5 circuits, main circuit main
module main (
  input  in_1,
  input  in_2,
  input  in_3,
  input  in_4,
  input  in_5,
  input  in_6,
  input  in_7,
  input  in_8,
  input  in_9,
  input  in_10,
  input  in_11,
  input  in_12,
  input  in_13,
  input  in_14,
  input  in_15,
  input  in_16,
  input  in_17,
  input  in_18,
  input  in_19,
  input  in_20,
  input  in_21,
  input  in_22,
  output out_23,
  output out_24,
  output out_25,
  output out_26,
  output out_27,
  output out_28,
  output out_29,
  output out_30,
  output out_31,
  output out_32,
  output out_33,
  output out_34,
  output out_35,
  output out_36
);

  wire n7404_1_gnd, n7408_1_gnd, n7432_1_gnd;

  _7408 u_7408_1 (
    ._1(in_1), ._2(in_4), ._3(out_24), ._4(in_7), ._5(in_12), ._6(out_28), .GND(n7408_1_gnd), .Vcc(1'b1),
    ._13(in_8), ._12(in_13), ._11(out_29), ._10(in_18), ._9(in_20), ._8(out_34));
  _7432 u_7432_1 (
    ._1(in_2), ._2(in_5), ._3(out_25), ._4(in_9), ._5(in_14), ._6(out_30), .GND(n7432_1_gnd), .Vcc(1'b1),
    ._13(in_10), ._12(in_15), ._11(out_31), ._10(in_19), ._9(in_21), ._8(out_35));
  _7404 u_7404_1 (
    ._1(in_3), ._2(out_23), ._3(in_6), ._4(out_26), ._5(in_16), ._6(out_32), .GND(n7404_1_gnd), .Vcc(1'b1),
    ._13(in_11), ._12(out_27), ._11(in_17), ._10(out_33), ._9(in_22), ._8(out_36));
  // also tied to GND on the sheet: {n7408_1_gnd, n7432_1_gnd, n7404_1_gnd}
endmodule

// NOT
module _7404 (
  input  Vcc,
  input  _1,
  input  _13,
  input  _3,
  input  _11,
  input  _5,
  input  _9,
  output _2,
  output _12,
  output _4,
  output _10,
  output _6,
  output _8,
  output GND
);

  Pull_Resistor pull_resistor_1 (.node(_2));
  Pull_Resistor pull_resistor_2 (.node(_4));
  Pull_Resistor pull_resistor_3 (.node(_6));
  Transistor transistor_1 (.in(Vcc), .out(_2), .gate(_1));
  Transistor #(.gate("br")) transistor_2 (.in(Vcc), .out(_12), .gate(_13));
  Pull_Resistor pull_resistor_4 (.node(_12));
  Transistor #(.gate("br")) transistor_3 (.in(Vcc), .out(_10), .gate(_11));
  Transistor transistor_4 (.in(Vcc), .out(_4), .gate(_3));
  Pull_Resistor pull_resistor_5 (.node(_10));
  Transistor #(.gate("br")) transistor_5 (.in(Vcc), .out(_8), .gate(_9));
  Transistor transistor_6 (.in(Vcc), .out(_6), .gate(_5));
  Pull_Resistor pull_resistor_6 (.node(_8));
endmodule

// AND
module _7408 (
  input  Vcc,
  input  _1,
  input  _13,
  input  _2,
  input  _12,
  input  _4,
  input  _10,
  input  _5,
  input  _9,
  output _3,
  output _11,
  output _6,
  output _8,
  output GND
);

  wire transistor_3_out, transistor_4_out, transistor_7_out, transistor_8_out;

  Pull_Resistor pull_resistor_1 (.node(_3));
  Pull_Resistor pull_resistor_2 (.node(_6));
  Transistor #(.\type ("n")) transistor_1 (.in(transistor_4_out), .out(_3), .gate(_1));
  Pull_Resistor pull_resistor_3 (.node(_11));
  Transistor #(.\type ("n"), .gate("br")) transistor_2 (.in(transistor_3_out), .out(_11), .gate(_13));
  Transistor #(.\type ("n"), .gate("br")) transistor_3 (.in(Vcc), .out(transistor_3_out), .gate(_12));
  Transistor #(.\type ("n")) transistor_4 (.in(Vcc), .out(transistor_4_out), .gate(_2));
  Pull_Resistor pull_resistor_4 (.node(_8));
  Transistor #(.\type ("n")) transistor_5 (.in(transistor_7_out), .out(_6), .gate(_4));
  Transistor #(.\type ("n"), .gate("br")) transistor_6 (.in(transistor_8_out), .out(_8), .gate(_10));
  Transistor #(.\type ("n")) transistor_7 (.in(Vcc), .out(transistor_7_out), .gate(_5));
  Transistor #(.\type ("n"), .gate("br")) transistor_8 (.in(Vcc), .out(transistor_8_out), .gate(_9));
endmodule

// OR
module _7432 (
  input  Vcc,
  input  _1,
  input  _13,
  input  _2,
  input  _12,
  input  _4,
  input  _10,
  input  _5,
  input  _9,
  output _3,
  output _11,
  output _6,
  output _8,
  output GND
);

  Pull_Resistor pull_resistor_1 (.node(_3));
  Pull_Resistor pull_resistor_2 (.node(_6));
  Transistor #(.\type ("n"), .gate("br")) transistor_1 (.in(Vcc), .out(_11), .gate(_13));
  Pull_Resistor pull_resistor_3 (.node(_11));
  Transistor #(.\type ("n")) transistor_2 (.in(Vcc), .out(_3), .gate(_1));
  Transistor #(.\type ("n")) transistor_3 (.in(Vcc), .out(_3), .gate(_2));
  Transistor #(.\type ("n"), .gate("br")) transistor_4 (.in(Vcc), .out(_11), .gate(_12));
  Transistor #(.\type ("n")) transistor_5 (.in(Vcc), .out(_6), .gate(_4));
  Pull_Resistor pull_resistor_4 (.node(_8));
  Transistor #(.\type ("n"), .gate("br")) transistor_6 (.in(Vcc), .out(_8), .gate(_10));
  Transistor #(.\type ("n")) transistor_7 (.in(Vcc), .out(_6), .gate(_5));
  Transistor #(.\type ("n"), .gate("br")) transistor_8 (.in(Vcc), .out(_8), .gate(_9));
endmodule

module tests (
  input  in_1,
  input  in_2,
  input  in_3,
  input  in_4,
  input  in_5,
  input  in_6,
  input  in_7,
  input  in_8,
  input  in_9,
  input  in_10,
  input  in_11,
  input  in_12,
  input  in_13,
  input  in_14,
  input  in_15,
  input  in_16,
  input  in_17,
  input  in_18,
  input  in_19,
  input  in_20,
  input  in_21,
  input  in_22,
  input  in_23,
  input  in_24,
  input  in_25,
  input  in_26,
  input  in_27,
  input  in_28,
  input  in_29,
  input  in_30,
  input  in_31,
  input  in_32,
  input  in_33,
  input  in_34,
  input  in_35,
  input  in_36,
  input  in_37,
  input  in_38,
  input  in_39,
  input  in_40,
  input  in_41,
  input  in_42,
  input  in_43,
  input  in_44,
  input  in_45,
  output out_46,
  output out_47,
  output out_48,
  output out_49,
  output out_50,
  output out_51,
  output out_52,
  output out_53,
  output out_54,
  output out_55,
  output out_56,
  output out_57,
  output NOT_Gate,
  output out_59,
  output out_60,
  output out_61,
  output out_62
);

  wire transistor_1_out, transistor_3_out, transistor_4_out, transistor_5_out, transistor_6_out,
       transistor_8_out, transistor_10_out, transistor_14_out, transistor_21_out, transistor_22_out,
       transistor_23_out, transistor_24_out, transistor_30_out, transistor_34_out, transistor_35_out,
       transistor_42_out, transistor_48_out, transistor_49_out, transistor_50_out, transistor_52_out,
       transistor_54_out, transistor_55_out;

  Transistor #(.\type ("n")) transistor_1 (.in(1'b1), .out(transistor_1_out), .gate(in_5));
  Pull_Resistor pull_resistor_1 (.node(out_46));
  Transistor #(.\type ("n")) transistor_2 (.in(transistor_1_out), .out(out_46), .gate(in_1));
  Transistor #(.\type ("n")) transistor_3 (.in(1'b1), .out(transistor_3_out), .gate(in_15));
  Transistor #(.\type ("n")) transistor_4 (.in(transistor_3_out), .out(transistor_4_out), .gate(in_11));
  Transistor #(.\type ("n")) transistor_5 (.in(1'b1), .out(transistor_5_out), .gate(in_29));
  Transistor #(.\type ("n")) transistor_6 (.in(transistor_5_out), .out(transistor_6_out), .gate(in_25));
  Pull_Resistor pull_resistor_2 (.node(NOT_Gate));
  Transistor transistor_7 (.in(1'b1), .out(NOT_Gate), .gate(in_37));
  Transistor #(.\type ("n")) transistor_8 (.in(1'b1), .out(transistor_8_out), .gate(in_43));
  Transistor transistor_9 (.in(transistor_8_out), .out(out_59), .gate(in_42));
  Transistor transistor_10 (.in(1'b1), .out(transistor_10_out), .gate(in_45));
  Transistor #(.\type ("n")) transistor_11 (.in(transistor_10_out), .out(out_61), .gate(in_44));
  Pull_Resistor pull_resistor_3 (.node(out_50));
  Transistor #(.\type ("n")) transistor_12 (.in(transistor_4_out), .out(out_50), .gate(in_9));
  Transistor #(.\type ("n")) transistor_13 (.in(transistor_14_out), .out(out_54), .gate(in_21));
  Pull_Resistor pull_resistor_4 (.node(out_54));
  Transistor #(.\type ("n")) transistor_14 (.in(transistor_6_out), .out(transistor_14_out), .gate(in_23));
  Transistor #(.\type ("n")) transistor_15 (.in(1'b1), .out(out_48), .gate(in_6));
  Transistor #(.\type ("n")) transistor_16 (.in(1'b1), .out(out_48), .gate(in_2));
  Pull_Resistor pull_resistor_5 (.node(out_48));
  Transistor #(.\type ("n")) transistor_17 (.in(1'b1), .out(out_52), .gate(in_19));
  Transistor #(.\type ("n")) transistor_18 (.in(1'b1), .out(out_52), .gate(in_16));
  Transistor #(.\type ("n")) transistor_19 (.in(1'b1), .out(out_56), .gate(in_33));
  Transistor #(.\type ("n")) transistor_20 (.in(1'b1), .out(out_56), .gate(in_35));
  Transistor #(.\type ("n")) transistor_21 (.in(1'b1), .out(transistor_21_out), .gate(in_40));
  Transistor #(.\type ("n")) transistor_22 (.in(transistor_23_out), .out(transistor_22_out), .gate(in_38));
  Pull_Resistor pull_resistor_6 (.node(transistor_22_out));
  Transistor #(.\type ("n")) transistor_23 (.in(1'b1), .out(transistor_23_out), .gate(in_40));
  Transistor transistor_24 (.in(1'b1), .out(transistor_24_out), .gate(transistor_22_out));
  Pull_Resistor pull_resistor_7 (.node(transistor_24_out));
  Transistor #(.\type ("n")) transistor_25 (.in(1'b1), .out(out_52), .gate(in_12));
  Pull_Resistor pull_resistor_8 (.node(out_52));
  Transistor #(.\type ("n")) transistor_26 (.in(1'b1), .out(out_56), .gate(in_30));
  Transistor #(.\type ("n")) transistor_27 (.in(1'b1), .out(out_56), .gate(in_26));
  Transistor #(.\type ("n")) transistor_28 (.in(1'b1), .out(transistor_21_out), .gate(in_38));
  Pull_Resistor pull_resistor_9 (.node(transistor_21_out));
  Pull_Resistor pull_resistor_10 (.node(out_60));
  Transistor #(.\type ("n")) transistor_29 (.in(transistor_30_out), .out(out_60), .gate(transistor_21_out));
  Transistor #(.\type ("n")) transistor_30 (.in(1'b1), .out(transistor_30_out), .gate(transistor_24_out));
  Pull_Resistor pull_resistor_11 (.node(out_56));
  Transistor transistor_31 (.in(1'b1), .out(out_49), .gate(in_7));
  Transistor transistor_32 (.in(1'b1), .out(out_53), .gate(in_20));
  Transistor transistor_33 (.in(1'b1), .out(out_57), .gate(in_36));
  Transistor transistor_34 (.in(1'b1), .out(transistor_34_out), .gate(in_41));
  Transistor transistor_35 (.in(1'b1), .out(transistor_35_out), .gate(in_41));
  Transistor transistor_36 (.in(1'b1), .out(out_49), .gate(in_3));
  Pull_Resistor pull_resistor_12 (.node(out_49));
  Transistor transistor_37 (.in(1'b1), .out(out_53), .gate(in_13));
  Transistor transistor_38 (.in(1'b1), .out(out_53), .gate(in_17));
  Pull_Resistor pull_resistor_13 (.node(out_53));
  Transistor transistor_39 (.in(1'b1), .out(out_57), .gate(in_31));
  Transistor transistor_40 (.in(1'b1), .out(out_57), .gate(in_34));
  Transistor transistor_41 (.in(1'b1), .out(transistor_34_out), .gate(in_39));
  Pull_Resistor pull_resistor_14 (.node(transistor_34_out));
  Transistor transistor_42 (.in(1'b1), .out(transistor_42_out), .gate(transistor_34_out));
  Transistor transistor_43 (.in(1'b1), .out(transistor_35_out), .gate(transistor_34_out));
  Transistor transistor_44 (.in(1'b1), .out(out_57), .gate(in_27));
  Pull_Resistor pull_resistor_15 (.node(out_57));
  Transistor transistor_45 (.in(1'b1), .out(transistor_42_out), .gate(in_39));
  Pull_Resistor pull_resistor_16 (.node(transistor_42_out));
  Pull_Resistor pull_resistor_17 (.node(transistor_35_out));
  Transistor transistor_46 (.in(1'b1), .out(out_62), .gate(transistor_42_out));
  Transistor transistor_47 (.in(1'b1), .out(out_62), .gate(transistor_35_out));
  Transistor transistor_48 (.in(1'b1), .out(transistor_48_out), .gate(in_8));
  Transistor transistor_49 (.in(1'b1), .out(transistor_49_out), .gate(in_18));
  Transistor transistor_50 (.in(1'b1), .out(transistor_50_out), .gate(in_32));
  Pull_Resistor pull_resistor_18 (.node(out_62));
  Transistor transistor_51 (.in(transistor_48_out), .out(out_47), .gate(in_4));
  Pull_Resistor pull_resistor_19 (.node(out_47));
  Transistor transistor_52 (.in(transistor_49_out), .out(transistor_52_out), .gate(in_14));
  Transistor transistor_53 (.in(transistor_52_out), .out(out_51), .gate(in_10));
  Pull_Resistor pull_resistor_20 (.node(out_51));
  Transistor transistor_54 (.in(transistor_55_out), .out(transistor_54_out), .gate(in_24));
  Transistor transistor_55 (.in(transistor_50_out), .out(transistor_55_out), .gate(in_28));
  Pull_Resistor pull_resistor_21 (.node(out_55));
  Transistor transistor_56 (.in(transistor_54_out), .out(out_55), .gate(in_22));

  // Notes on the sheet:
  //   AND Gates
  //   OR Gates
  //   XOR Gate 1
  //   NAND Gates
  //   XOR Gate 2 (w/ NAND)
  //   NOR Gates
endmodule
